// Logisim project alu.circ as structural Verilog: 1 circuit, main circuit main
module main (
  input  [15:0] X,
  input  [15:0] Y,
  input  [2:0] Switch,
  output Equal,
  output [15:0] Result,
  output [15:0] Result_2,
  output Signed_Overflow
);

  wire comparator_1_lt, comparator_2_eq, comparator_3_eq, comparator_4_eq, overflow;
  wire [3:0] bit_extender_2_out, bit_extender_3_out;
  wire [15:0] add, addu, \and , mult, \or , sll, slt, srt;

  Adder #(.width(16)) adder_1 (.a(X), .b(Y), .out(add));  // open: cin, cout
  assign \and  = X & Y;  // AND_Gate and_1, 16 bits wide
  assign \or  = X | Y;  // OR_Gate or_1, 16 bits wide
  Comparator #(.width(16)) comparator_1 (.a(X), .b(Y), .eq(Equal), .lt(comparator_1_lt));  // open: gt
  assign slt = {{15{1'b0}}, comparator_1_lt};  // Bit_Extender bit_extender_1
  Comparator #(.width(3)) comparator_2 (.a({add[15], Y[15], X[15]}), .b(3'b100), .eq(comparator_2_eq));  // open: gt, lt
  Comparator #(.width(3)) comparator_3 (.a({add[15], Y[15], X[15]}), .b(3'b011), .eq(comparator_3_eq));  // open: gt, lt
  Adder #(.width(16)) adder_2 (.a(X), .b(Y), .out(addu));  // open: cin, cout
  or or_2 (overflow, comparator_2_eq, comparator_3_eq);
  Shifter #(.width(16)) shifter_1 (.in(X), .\dist (bit_extender_2_out), .out(sll));
  Bit_Extender #(.in_width(16), .out_width(4)) bit_extender_2 (.in(Y), .out(bit_extender_2_out));
  Shifter #(.width(16), .shift("lr")) shifter_2 (.in(X), .\dist (bit_extender_3_out), .out(srt));
  Bit_Extender #(.in_width(16), .out_width(4)) bit_extender_3 (.in(Y), .out(bit_extender_3_out));
  Multiplier #(.width(16)) multiplier_1 (.a(X), .b(Y), .out(mult), .cout(Result_2));  // open: cin
  Multiplexer #(.select(3), .width(16), .enable("false")) multiplexer_1 (
    .in0(sll), .in1(srt), .in2(add), .in3(\and ), .in4(\or ), .in5(addu), .in6(slt), .in7(mult),
    .out(Result), .sel(Switch));
  Comparator #(.width(3)) comparator_4 (.a(Switch), .b(3'b010), .eq(comparator_4_eq));  // open: gt, lt
  and and_2 (Signed_Overflow, overflow, comparator_4_eq);

  // Other names for the same wires on the sheet: S[2:0] = Switch; signs[2:0] = {add[15], Y[15], X[15]}

  // Notes on the sheet:
  //   INPUTS to your circuit
  //   DON'T CHANGE THE LOCATIONS OF THE INPUTS AND OUTPUTS!
  //   OUTPUTS from your circuit
endmodule
