// Logisim project cpu.circ as structural Verilog: 4 circuits, main circuit main
module main (
  input  [15:0] INSTRUCTION,
  input  CLOCK,
  output [15:0] FETCH_ADDRESS,
  output Overflow,
  output [15:0] s0_Value,
  output [15:0] s1_Value,
  output [15:0] s2_Value,
  output [15:0] ra_Value,
  output [15:0] sp_Value,
  output [15:0] HI_Value,
  output [15:0] LO_Value
);

  wire and_1_out, and_2_out, and_3_out, C_ALUSrc, C_ImmExType, C_IsBeq, C_IsBne, C_IsJmp, C_IsU, C_JmpType,
       C_LOSrc, C_MemWrEn, C_ReadReg2, C_RegWrEn, C_WrHIEn, C_WrLOEn, Equal, MEM_p1, MEM_p3, MEM_p8, MEM_p12,
       not_1_out, not_2_out, or_1_out, TakeBranch;
  wire [1:0] decoder_1_rd_u;
  wire [2:0] C_ALUCtr, C_RegWrBkSrc, decoder_1_rd, funct, multiplexer_7_out, rd, rs, rt;
  wire [3:0] op;
  wire [5:0] Imm6;
  wire [15:0] adder_1_out, ALURst, BranchAdr, Imm16, Imm_lui, INSTRUCTION_2, JmpAdr, main_1_read_data_1,
       MEM_p10, MUL_HI, multiplexer_1_out, multiplexer_2_out, multiplexer_3_out, multiplexer_4_out,
       multiplexer_5_out, multiplexer_8_out, PC, PC_2, WD, WriteBack;

  or or_1 (or_1_out, TakeBranch, C_IsJmp);
  Register #(.width(16)) MidPCReg (.D(FETCH_ADDRESS), .Q(PC), .clk(CLOCK));  // open: en, clr
  Multiplexer #(.width(16), .enable("false")) multiplexer_1 (
    .in0(INSTRUCTION), .in1({16{1'b0}}), .out(multiplexer_1_out), .sel(or_1_out));
  Register #(.width(16)) MidINSTReg (.D(multiplexer_1_out), .Q(INSTRUCTION_2), .clk(CLOCK));  // open: en, clr
  Register #(.width(16)) HI (.D(MUL_HI), .en(C_WrHIEn), .Q(HI_Value), .clk(CLOCK));  // open: clr
  decoder decoder_1 (
    .INPUT_Instruction(INSTRUCTION_2), .FUNCT(funct), .RT(rt), .RS(rs), .RD(decoder_1_rd),
    .RD_U(decoder_1_rd_u), .OP(op), .IMM(Imm6), .IMM_lui(Imm_lui), .IMM_jmp(JmpAdr), .PC(PC));
  Adder #(.width(16)) adder_1 (.a(FETCH_ADDRESS), .b(16'h2), .out(adder_1_out));  // open: cin, cout
  Multiplexer #(.width(16), .enable("false")) multiplexer_2 (
    .in0(adder_1_out), .in1(BranchAdr), .out(multiplexer_2_out), .sel(TakeBranch));
  Multiplexer #(.width(16), .enable("false")) multiplexer_3 (
    .in0(multiplexer_2_out), .in1(multiplexer_4_out), .out(multiplexer_3_out), .sel(C_IsJmp));
  Multiplexer #(.width(16), .enable("false")) multiplexer_4 (
    .in0(JmpAdr), .in1(ALURst), .out(multiplexer_4_out), .sel(C_JmpType));
  Register #(.width(16)) u_PC (.D(multiplexer_3_out), .Q(FETCH_ADDRESS), .clk(CLOCK));  // open: en, clr
  Multiplexer #(.width(16), .enable("false")) multiplexer_5 (
    .in0(ALURst), .in1(Imm_lui), .out(multiplexer_5_out), .sel(C_LOSrc));
  Register #(.width(16)) LO (.D(multiplexer_5_out), .en(C_WrLOEn), .Q(LO_Value), .clk(CLOCK));  // open: clr
  Multiplexer #(.width(3), .enable("false")) multiplexer_6 (
    .in0(decoder_1_rd), .in1({1'b0, decoder_1_rd_u}), .out(rd), .sel(C_IsU));
  exImm eximm_1 (.IMM(Imm6), .Zero_Signed(C_ImmExType), .To_Instr_Mem(Imm16));
  Adder #(.width(16)) adder_2 (.a(PC), .b(Imm16), .out(BranchAdr));  // open: cin, cout
  Multiplexer #(.width(3), .enable("false")) multiplexer_7 (
    .in0(rt), .in1(rd), .out(multiplexer_7_out), .sel(C_ReadReg2));
  and and_1 (and_1_out, C_IsBeq, Equal);
  and and_2 (and_2_out, C_IsBne, not_1_out);
  not not_1 (not_1_out, Equal);
  and and_3 (and_3_out, C_RegWrEn, not_2_out);
  or or_2 (TakeBranch, and_1_out, and_2_out);
  regfile_main main_1 (
    .Read_Register_1(rs), .Read_Register_2(multiplexer_7_out), .Write_Register(rd), .Write_Data(WriteBack),
    .Write_Enable(and_3_out), .Clock(CLOCK), .Read_Data_1(main_1_read_data_1), .Read_Data_2(WD),
    .s0_Value(s0_Value), .s1_Value(s1_Value), .s2_Value(s2_Value), .ra_Value(ra_Value), .sp_Value(sp_Value));
  not not_2 (not_2_out, Overflow);
  Multiplexer #(.width(16), .enable("false")) multiplexer_8 (
    .in0(WD), .in1(Imm16), .out(multiplexer_8_out), .sel(C_ALUSrc));
  alu_main main_2 (
    .Switch(C_ALUCtr), .X(main_1_read_data_1), .Equal(Equal), .Result(ALURst), .Y(multiplexer_8_out),
    .Result_2(MUL_HI), .Signed_Overflow(Overflow));
  control_unit control_unit_1 (
    .Opcode(op), .Funct(funct), .C_IsJmp(C_IsJmp), .C_WrHIEn(C_WrHIEn), .C_JmpType(C_JmpType),
    .C_LOSrc(C_LOSrc), .C_WrLOEn(C_WrLOEn), .C_IsU(C_IsU), .C_ImmExType(C_ImmExType),
    .C_ReadReg2(C_ReadReg2), .C_IsBeq(C_IsBeq), .C_IsBne(C_IsBne), .C_RegWrEn(C_RegWrEn),
    .C_ALUSrc(C_ALUSrc), .C_ALUCtrl(C_ALUCtr), .C_MemWrEn(C_MemWrEn), .C_RegWrBkSrc(C_RegWrBkSrc));
  Adder #(.width(16)) adder_3 (.a(PC), .b(16'h2), .out(PC_2));  // open: cin, cout
  // mem_main MEM: pin names not known; wires that end beside it: MEM_p1, MEM_p1, MEM_p3, MEM_p3, ALURst, WD, C_MemWrEn, MEM_p8, CLOCK, MEM_p10, MEM_p8, MEM_p12
  Multiplexer #(.select(3), .width(16), .disabled(0), .enable("false")) multiplexer_9 (
    .in0(ALURst), .in1(MEM_p10), .in2(PC_2), .in3(LO_Value), .in4(HI_Value), .out(WriteBack),
    .sel(C_RegWrBkSrc));  // open: in5, in6, in7

  // Other names for the same wires on the sheet: clk = CLOCK; fetch_addr[15:0] = FETCH_ADDRESS; HI[15:0] = HI_Value;
  //   LO[15:0] = LO_Value; ra[15:0] = ra_Value; s0[15:0] = s0_Value; s1[15:0] = s1_Value; s2[15:0] = s2_Value;
  //   sp[15:0] = sp_Value

  // Notes on the sheet:
  //   Output
  //   These are outputs/inputs from run.circ
  //   Inputs
  //   These are DEBUG/TEST outputs from your circuit.
endmodule

// CONTROL UNIT
module control_unit (
  input  [3:0] Opcode,
  input  [2:0] Funct,
  output C_IsJmp,
  output C_WrHIEn,
  output C_JmpType,
  output C_LOSrc,
  output C_WrLOEn,
  output C_IsU,
  output C_ImmExType,
  output C_ReadReg2,
  output C_IsBeq,
  output C_IsBne,
  output C_RegWrEn,
  output C_ALUSrc,
  output [2:0] C_ALUCtrl,
  output C_MemWrEn,
  output [2:0] C_RegWrBkSrc
);

  wire add, addi, addiu, addu, \and , andi, comparator_16_eq, comparator_17_eq, comparator_18_eq,
       comparator_19_eq, comparator_20_eq, comparator_21_eq, comparator_22_eq, comparator_23_eq, j, lh, mflo,
       op_5, \or , ori, R, sll, slt, slti, srl;

  Comparator #(.width(4)) comparator_1 (.a(Opcode), .b(4'b0000), .eq(R));  // open: gt, lt
  Comparator #(.width(4)) comparator_2 (.a(Opcode), .b(4'b0001), .eq(C_LOSrc));  // open: gt, lt
  Comparator #(.width(4)) comparator_3 (.a(Opcode), .b(4'b0010), .eq(j));  // open: gt, lt
  Comparator #(.width(4)) comparator_4 (.a(Opcode), .b(4'b0011), .eq(C_JmpType));  // open: gt, lt
  Comparator #(.width(4)) comparator_5 (.a(Opcode), .b(4'b0100), .eq(C_IsBeq));  // open: gt, lt
  Comparator #(.width(4), .mode("unsigned")) comparator_6 (
    .a(Opcode), .b(4'b0101), .gt(op_5), .eq(C_IsBne));  // open: lt
  Comparator #(.width(4)) comparator_7 (.a(Opcode), .b(4'b0110), .eq(addi));  // open: gt, lt
  Comparator #(.width(4)) comparator_8 (.a(Opcode), .b(4'b0111), .eq(addiu));  // open: gt, lt
  Comparator #(.width(4)) comparator_9 (.a(Opcode), .b(4'b1000), .eq(slti));  // open: gt, lt
  Comparator #(.width(4)) comparator_10 (.a(Opcode), .b(4'b1001), .eq(andi));  // open: gt, lt
  Comparator #(.width(4)) comparator_11 (.a(Opcode), .b(4'b1010), .eq(ori));  // open: gt, lt
  Comparator #(.width(4)) comparator_12 (.a(Opcode), .b(4'b1011), .eq(lh));  // open: gt, lt
  Comparator #(.width(4)) comparator_13 (.a(Opcode), .b(4'b1100), .eq(C_MemWrEn));  // open: gt, lt
  Comparator #(.width(4)) comparator_14 (.a(Opcode), .b(4'b1101), .eq(C_RegWrBkSrc[2]));  // open: gt, lt
  Comparator #(.width(4)) comparator_15 (.a(Opcode), .b(4'b1110), .eq(mflo));  // open: gt, lt
  or or_1 (C_IsJmp, j, C_JmpType);
  and and_1 (sll, R, comparator_16_eq);
  Comparator #(.width(3)) comparator_16 (.a(Funct), .b(3'b000), .eq(comparator_16_eq));  // open: gt, lt
  and and_2 (srl, R, comparator_17_eq);
  Comparator #(.width(3)) comparator_17 (.a(Funct), .b(3'b001), .eq(comparator_17_eq));  // open: gt, lt
  and and_3 (add, R, comparator_18_eq);
  Comparator #(.width(3)) comparator_18 (.a(Funct), .b(3'b010), .eq(comparator_18_eq));  // open: gt, lt
  and and_4 (\and , R, comparator_19_eq);
  Comparator #(.width(3)) comparator_19 (.a(Funct), .b(3'b011), .eq(comparator_19_eq));  // open: gt, lt
  and and_5 (\or , R, comparator_20_eq);
  Comparator #(.width(3)) comparator_20 (.a(Funct), .b(3'b100), .eq(comparator_20_eq));  // open: gt, lt
  and and_6 (addu, R, comparator_21_eq);
  Comparator #(.width(3)) comparator_21 (.a(Funct), .b(3'b101), .eq(comparator_21_eq));  // open: gt, lt
  and and_7 (slt, R, comparator_22_eq);
  Comparator #(.width(3)) comparator_22 (.a(Funct), .b(3'b110), .eq(comparator_22_eq));  // open: gt, lt
  and and_8 (C_WrHIEn, R, comparator_23_eq);
  Comparator #(.width(3)) comparator_23 (.a(Funct), .b(3'b111), .eq(comparator_23_eq));  // open: gt, lt
  or or_2 (C_WrLOEn, C_WrHIEn, C_LOSrc);
  or or_3 (C_IsU, C_LOSrc, j);
  or or_4 (C_ImmExType, C_JmpType, C_IsBeq, C_IsBne, addi, addiu, slti, lh, C_MemWrEn);
  or or_5 (C_ReadReg2, C_IsBeq, C_IsBne, C_MemWrEn);
  nor nor_1 (C_RegWrEn, C_WrHIEn, C_LOSrc, C_IsBeq, C_IsBne, C_MemWrEn);
  or or_6 (C_ALUCtrl[2], \or , addu, slt, C_WrHIEn, addiu, slti, ori, lh, C_MemWrEn, C_JmpType);
  or or_7 (C_ALUCtrl[1], add, \and , slt, C_WrHIEn, addi, slti, andi);
  or or_8 (C_ALUCtrl[0], srl, \and , addu, C_WrHIEn, C_JmpType, addiu, andi, lh, C_MemWrEn);
  or or_9 (C_ALUSrc, C_JmpType, op_5);
  or or_10 (C_RegWrBkSrc[1], j, C_JmpType, mflo);
  or or_11 (C_RegWrBkSrc[0], lh, mflo);

  // Other names for the same wires on the sheet: beq = C_IsBeq; bne = C_IsBne; ALUCtrl0 = C_ALUCtrl[0];
  //   ALUCtrl1 = C_ALUCtrl[1]; ALUCtrl2 = C_ALUCtrl[2]; RWBS0 = C_RegWrBkSrc[0]; RWBS1 = C_RegWrBkSrc[1];
  //   mfhi = C_RegWrBkSrc[2]; RWBS2 = C_RegWrBkSrc[2]; jr = C_JmpType; lui = C_LOSrc; mult = C_WrHIEn;
  //   op[3:0] = Opcode; sh = C_MemWrEn
endmodule

// DECODER
module decoder (
  input  [15:0] INPUT_Instruction,
  input  [15:0] PC,
  output [2:0] RT,
  output [2:0] RS,
  output [2:0] RD,
  output [1:0] RD_U,
  output [5:0] IMM,
  output [15:0] IMM_lui,
  output [15:0] IMM_jmp,
  output [2:0] FUNCT,
  output [3:0] OP
);


  assign FUNCT = INPUT_Instruction[2:0];
  assign IMM = INPUT_Instruction[5:0];
  assign IMM_jmp = {PC[15:10], INPUT_Instruction[9:0]};
  assign IMM_lui = {INPUT_Instruction[9:0], {6{1'b0}}};
  assign OP = INPUT_Instruction[15:12];
  assign RD = INPUT_Instruction[11:9];
  assign RD_U = INPUT_Instruction[11:10];
  assign RS = INPUT_Instruction[8:6];
  assign RT = INPUT_Instruction[5:3];

  // Other names for the same wires on the sheet: Imm_U[9:0] = INPUT_Instruction[9:0];
  //   Opcode[3:0] = INPUT_Instruction[15:12]
endmodule

// Extender
module exImm (
  input  [5:0] IMM,
  input  Zero_Signed,
  output [15:0] To_Instr_Mem
);

  wire [15:0] bit_extender_1_out, bit_extender_2_out;

  assign bit_extender_1_out = {{10{1'b0}}, IMM};  // Bit_Extender bit_extender_1
  assign bit_extender_2_out = {{10{IMM[5]}}, IMM};  // Bit_Extender bit_extender_2
  Multiplexer #(.width(16), .enable("false")) multiplexer_1 (
    .in0(bit_extender_1_out), .in1(bit_extender_2_out), .out(To_Instr_Mem), .sel(Zero_Signed));
endmodule
