// Logisim project alu-slteq.circ as structural Verilog: 1 circuit, main circuit main
module main (
  output [7:0] Test_num,
  output halt,
  output Equal,
  output [15:0] Result,
  output Signed_Overflow,
  output [15:0] Result_2
);

  wire clock_1_out;
  wire [2:0] rom_3_data;
  wire [7:0] adder_1_out;
  wire [15:0] rom_1_data, rom_2_data;

  Clock clock_1 (.out(clock_1_out));
  Adder adder_1 (.a(8'h1), .b(Test_num), .out(adder_1_out));  // open: cin, cout
  Register register_1 (.D(adder_1_out), .Q(Test_num), .clk(clock_1_out));  // open: en, clr
  Comparator #(.mode("unsigned")) comparator_1 (.a(8'h8), .b(Test_num), .eq(halt));  // open: gt, lt
  ROM #(.dataWidth(16)) rom_1 (.addr(Test_num), .data(rom_1_data));  // open: sel
  ROM #(.dataWidth(16)) rom_2 (.addr(Test_num), .data(rom_2_data));  // open: sel
  ROM #(.dataWidth(3)) rom_3 (.addr(Test_num), .data(rom_3_data));  // open: sel
  alu_main main_1 (
    .Switch(rom_3_data), .X(rom_1_data), .Equal(Equal), .Result(Result), .Y(rom_2_data), .Result_2(Result_2),
    .Signed_Overflow(Signed_Overflow));

  // Notes on the sheet:
  //   contents of rom_1 (hex, n*v repeats v):
  //   ffff 0 dead beef 7fff 6b6b 8000 8001
  //   contents of rom_2 (hex, n*v repeats v):
  //   0 ffff dead beef 7ffe 6c00 8001 8000
  //   contents of rom_3 (hex, n*v repeats v):
  //   8*6
  //   YOUR ALU SHOULD FIT HERE
  //   There should be no blue/red wires here, and the result shouldn't be x's.
endmodule
