// Logisim project regfile.circ as structural Verilog: 1 circuit, main circuit main
module main (
  input  [2:0] Read_Register_1,
  input  [2:0] Read_Register_2,
  input  [2:0] Write_Register,
  input  [15:0] Write_Data,
  input  Write_Enable,
  input  Clock,
  output [15:0] s0_Value,
  output [15:0] s1_Value,
  output [15:0] s2_Value,
  output [15:0] ra_Value,
  output [15:0] sp_Value,
  output [15:0] Read_Data_1,
  output [15:0] Read_Data_2
);

  wire and_1_out, w_a0, w_ra, w_S0, w_S1, w_sp, w_v0, w_zero;
  wire [15:0] a0, v0, zero;

  and and_1 (and_1_out, 1'b0, w_zero);
  Register #(.width(16)) S0 (.D(Write_Data), .en(w_S0), .Q(s0_Value), .clk(Clock));  // open: clr
  Register #(.width(16)) u_zero (.D(Write_Data), .en(and_1_out), .Q(zero), .clk(Clock));  // open: clr
  Demultiplexer #(.select(3), .enable("false")) demultiplexer_1 (
    .out0(w_zero), .out1(w_ra), .out2(w_S0), .out3(w_S1), .out4(w_a0), .out5(w_a0), .out6(w_v0), .out7(w_sp),
    .in(Write_Enable), .sel(Write_Register));
  Register #(.width(16)) S1 (.D(Write_Data), .en(w_S1), .Q(s1_Value), .clk(Clock));  // open: clr
  Multiplexer #(.select(3), .width(16), .enable("false")) multiplexer_1 (
    .in0(zero), .in1(ra_Value), .in2(s0_Value), .in3(s1_Value), .in4(s2_Value), .in5(a0), .in6(v0),
    .in7(sp_Value), .out(Read_Data_1), .sel(Read_Register_1));
  Register #(.width(16)) S2 (.D(Write_Data), .en(w_a0), .Q(s2_Value), .clk(Clock));  // open: clr
  Register #(.width(16)) u_a0 (.D(Write_Data), .en(w_a0), .Q(a0), .clk(Clock));  // open: clr
  Register #(.width(16)) ra (.D(Write_Data), .en(w_ra), .Q(ra_Value), .clk(Clock));  // open: clr
  Register #(.width(16)) u_v0 (.D(Write_Data), .en(w_v0), .Q(v0), .clk(Clock));  // open: clr
  Multiplexer #(.select(3), .width(16), .enable("false")) multiplexer_2 (
    .in0(zero), .in1(ra_Value), .in2(s0_Value), .in3(s1_Value), .in4(s2_Value), .in5(a0), .in6(v0),
    .in7(sp_Value), .out(Read_Data_2), .sel(Read_Register_2));
  Register #(.width(16)) sp (.D(Write_Data), .en(w_sp), .Q(sp_Value), .clk(Clock));  // open: clr

  // Other names for the same wires on the sheet: clk = Clock; ra[15:0] = ra_Value; read_data1[15:0] = Read_Data_1;
  //   read_data2[15:0] = Read_Data_2; read_reg1[2:0] = Read_Register_1; read_reg2[2:0] = Read_Register_2;
  //   S0[15:0] = s0_Value; S1[15:0] = s1_Value; S2[15:0] = s2_Value; sp[15:0] = sp_Value; w_S2 = w_a0;
  //   write_en = Write_Enable; write_reg[2:0] = Write_Register

  // Notes on the sheet:
  //   INPUTS to your circuit
  //   DON'T CHANGE THE LOCATIONS OF THE INPUTS AND OUTPUTS!
  //   These are DEBUG/TEST outputs from your circuit.
  //   OUTPUTS from your circuit
endmodule
